// Logisim project 32 bits OR Gate.circ as structural Verilog: 1 circuit, main circuit main
module main (
  input  [31:0] input_one,
  input  [31:0] input_two,
  output [31:0] OR
);

  or or_1 (OR[0], input_one[0], input_two[0]);
  or or_2 (OR[1], input_one[1], input_two[1]);
  or or_3 (OR[2], input_one[2], input_two[2]);
  or or_4 (OR[3], input_one[3], input_two[3]);
  or or_5 (OR[4], input_one[4], input_two[4]);
  or or_6 (OR[5], input_one[5], input_two[5]);
  or or_7 (OR[6], input_one[6], input_two[6]);
  or or_8 (OR[7], input_one[7], input_two[7]);
  or or_9 (OR[8], input_one[8], input_two[8]);
  or or_10 (OR[9], input_one[9], input_two[9]);
  or or_11 (OR[10], input_one[10], input_two[10]);
  or or_12 (OR[11], input_one[11], input_two[11]);
  or or_13 (OR[12], input_one[12], input_two[12]);
  or or_14 (OR[13], input_one[13], input_two[13]);
  or or_15 (OR[14], input_one[14], input_two[14]);
  or or_16 (OR[15], input_one[15], input_two[15]);
  or or_17 (OR[16], input_one[16], input_two[16]);
  or or_18 (OR[17], input_one[17], input_two[17]);
  or or_19 (OR[18], input_one[18], input_two[18]);
  or or_20 (OR[19], input_one[19], input_two[19]);
  or or_21 (OR[20], input_one[20], input_two[20]);
  or or_22 (OR[21], input_one[21], input_two[21]);
  or or_23 (OR[22], input_one[22], input_two[22]);
  or or_24 (OR[23], input_one[23], input_two[23]);
  or or_25 (OR[24], input_one[24], input_two[24]);
  or or_26 (OR[25], input_one[25], input_two[25]);
  or or_27 (OR[26], input_one[26], input_two[26]);
  or or_28 (OR[27], input_one[27], input_two[27]);
  or or_29 (OR[28], input_one[28], input_two[28]);
  or or_30 (OR[29], input_one[29], input_two[29]);
  or or_31 (OR[30], input_one[30], input_two[30]);
  or or_32 (OR[31], input_one[31], input_two[31]);
endmodule
