// Logisim project ALU.circ as structural Verilog: 1 circuit, main circuit main
module main (
  input  [31:0] Input_one,
  input  [31:0] Input_two,
  input  [5:0] ALu_Op,
  output [31:0] Result
);

  wire [31:0] adder_1_out, divider_1_out, main_1_or, main_2_and, multiplier_1_out, subtractor_1_out;

  Adder #(.width(32)) adder_1 (.a(Input_one), .b(Input_two), .out(adder_1_out));  // open: cin, cout
  Subtractor #(.width(32)) subtractor_1 (.a(Input_one), .b(Input_two), .out(subtractor_1_out));  // open: bin, bout
  Multiplier #(.width(32)) multiplier_1 (.a(Input_one), .b(Input_two), .out(multiplier_1_out));  // open: cin, cout
  Divider #(.width(32)) divider_1 (.a(Input_one), .b(Input_two), .out(divider_1_out));  // open: upper, rem
  _32_bits_OR_Gate_main main_1 (.input_one(Input_one), .input_two(Input_two), .OR(main_1_or));
  _32_bits_AND_Gate_main main_2 (.input_one(Input_one), .input_two(Input_two), .And(main_2_and));
  Multiplexer #(.select(5), .width(32), .disabled(0)) multiplexer_1 (
    .in0(adder_1_out), .in1(subtractor_1_out), .in2(multiplier_1_out), .in3(divider_1_out), .in4(main_1_or),
    .in5(main_2_and), .out(Result), .sel(ALu_Op[4:0]));  // open: in6, in7, in8, in9, in10, in11, in12, in13, in14, in15, in16, in17, in18, in19, in20, in21, in22, in23, in24, in25, in26, in27, in28, in29, in30, in31, en
endmodule
