// Logisim project 32 bits AND Gate.circ as structural Verilog: 1 circuit, main circuit main
module main (
  input  [31:0] input_one,
  input  [31:0] input_two,
  output [31:0] And
);

  and and_1 (And[0], input_one[0], input_two[0]);
  and and_2 (And[1], input_one[1], input_two[1]);
  and and_3 (And[2], input_one[2], input_two[2]);
  and and_4 (And[3], input_one[3], input_two[3]);
  and and_5 (And[4], input_one[4], input_two[4]);
  and and_6 (And[5], input_one[5], input_two[5]);
  and and_7 (And[6], input_one[6], input_two[6]);
  and and_8 (And[7], input_one[7], input_two[7]);
  and and_9 (And[8], input_one[8], input_two[8]);
  and and_10 (And[9], input_one[9], input_two[9]);
  and and_11 (And[10], input_one[10], input_two[10]);
  and and_12 (And[11], input_one[11], input_two[11]);
  and and_13 (And[12], input_one[12], input_two[12]);
  and and_14 (And[13], input_one[13], input_two[13]);
  and and_15 (And[14], input_one[14], input_two[14]);
  and and_16 (And[15], input_one[15], input_two[15]);
  and and_17 (And[16], input_one[16], input_two[16]);
  and and_18 (And[17], input_one[17], input_two[17]);
  and and_19 (And[18], input_one[18], input_two[18]);
  and and_20 (And[19], input_one[19], input_two[19]);
  and and_21 (And[20], input_one[20], input_two[20]);
  and and_22 (And[21], input_one[21], input_two[21]);
  and and_23 (And[22], input_one[22], input_two[22]);
  and and_24 (And[23], input_one[23], input_two[23]);
  and and_25 (And[24], input_one[24], input_two[24]);
  and and_26 (And[25], input_one[25], input_two[25]);
  and and_27 (And[26], input_one[26], input_two[26]);
  and and_28 (And[27], input_one[27], input_two[27]);
  and and_29 (And[28], input_one[28], input_two[28]);
  and and_30 (And[29], input_one[29], input_two[29]);
  and and_31 (And[30], input_one[30], input_two[30]);
  and and_32 (And[31], input_one[31], input_two[31]);
endmodule
