// Logisim project CPU.circ as structural Verilog: 1 circuit, main circuit main
module main (
);

  wire main_1_p2, main_1_p3, main_1_p4, main_1_p5, main_1_p6, main_1_p7, main_1_p9, main_1_p10, main_1_p11,
       main_4_zeroflag;
  wire [4:0] multiplexer_1_out;
  wire [5:0] main_1_p8;
  wire [31:0] main_2_rs_output, main_2_rt_output, main_3_result, main_4_result, main_5_jumped_address,
       main_6_result, multiplexer_2_out, multiplexer_3_out, multiplexer_4_out, PC_q, ram_1_data, ram_2_data;

  Register #(.width(32)) PC (.D(multiplexer_3_out), .Q(PC_q));  // open: en, clk, clr
  RAM #(.addrWidth(24), .dataWidth(32)) ram_1 (.addr(PC_q[23:0]), .data(ram_1_data));  // open: sel, clk, ld, clr
  // Control_Unit_main main_1: pin names not known; wires that end beside it: ram_1_data, main_1_p2, main_1_p3, main_1_p4, main_1_p5, main_1_p6, main_1_p7, main_1_p8, main_1_p9, main_1_p10, main_1_p11
  Multiplexer #(.width(5), .enable("false")) multiplexer_1 (
    .in0(ram_1_data[20:16]), .in1(ram_1_data[15:11]), .out(multiplexer_1_out), .sel(main_1_p4));
  Register_File_main main_2 (
    .Rs_Output(main_2_rs_output), .Rt_Output(main_2_rt_output), .Rs(ram_1_data[25:21]),
    .Rt(ram_1_data[20:16]), .Reg_Write(main_1_p6), .Rd(multiplexer_1_out), .Write_Data(multiplexer_4_out));  // open: Clock
  Extension_Unit_main main_3 (.\input (ram_1_data[15:0]), .Result(main_3_result), .ExOp(main_1_p7));
  Multiplexer #(.width(32), .enable("false")) multiplexer_2 (
    .in0(main_2_rt_output), .in1(main_3_result), .out(multiplexer_2_out), .sel(main_1_p5));
  ALU_main main_4 (
    .Input_one(main_2_rs_output), .Input_two(multiplexer_2_out), .ALu_Op(main_1_p8), .Result(main_4_result),
    .Zeroflag(main_4_zeroflag));
  jump_unit_main main_5 (.\input (PC_q), .jumped_Address(main_5_jumped_address));
  branch_unit_main main_6 (
    .pc(PC_q), .immediate(main_3_result), .zeroRes(main_4_zeroflag), .branchRes(main_1_p3),
    .Result(main_6_result));
  RAM #(.addrWidth(24), .dataWidth(32), .bus("separate")) ram_2 (
    .addr(main_4_result[23:0]), .din(main_2_rt_output), .data(ram_2_data), .str(main_1_p9), .ld(main_1_p10));  // open: sel, clk, clr
  Multiplexer #(.width(32), .enable("false")) multiplexer_3 (
    .in0(main_5_jumped_address), .in1(main_6_result), .out(multiplexer_3_out), .sel(main_1_p2));
  Multiplexer #(.width(32), .enable("false")) multiplexer_4 (
    .in0(main_4_result), .in1(ram_2_data), .out(multiplexer_4_out), .sel(main_1_p11));
endmodule
