// Logisim project Control Unit.circ as structural Verilog: 1 circuit, main circuit main
module main (
  input  [5:0] OP_Code,
  output [5:0] OP_Code_2,
  output RegDes,
  output ALUsrc,
  output RegWrite,
  output jump,
  output branch,
  output MemWrite,
  output MemRead,
  output MemToReg,
  output ExOp
);

  wire addi_out, andi_out, divi_out, muli_out, ori_out, subi_out;

  and addi (addi_out, ~OP_Code[0], OP_Code[1], OP_Code[2], ~OP_Code[3], ~OP_Code[4]);  // AND_Gate
  and subi (subi_out, OP_Code[0], OP_Code[1], OP_Code[2], ~OP_Code[3], ~OP_Code[4]);  // AND_Gate
  and muli (muli_out, ~OP_Code[0], ~OP_Code[1], ~OP_Code[2], OP_Code[3], ~OP_Code[4]);  // AND_Gate
  and divi (divi_out, OP_Code[0], ~OP_Code[1], ~OP_Code[2], OP_Code[3], ~OP_Code[4]);  // AND_Gate
  and ori (ori_out, ~OP_Code[0], OP_Code[1], ~OP_Code[2], OP_Code[3], ~OP_Code[4]);  // AND_Gate
  and andi (andi_out, OP_Code[0], OP_Code[1], ~OP_Code[2], OP_Code[3], ~OP_Code[4]);  // AND_Gate
  and lw (MemRead, ~OP_Code[0], ~OP_Code[1], OP_Code[2], OP_Code[3], ~OP_Code[4]);  // AND_Gate
  and sw (MemWrite, OP_Code[0], ~OP_Code[1], OP_Code[2], OP_Code[3], ~OP_Code[4]);  // AND_Gate
  and beq (branch, ~OP_Code[0], OP_Code[1], OP_Code[2], OP_Code[3], ~OP_Code[4]);  // AND_Gate
  and u_jump (jump, OP_Code[0], OP_Code[1], OP_Code[2], OP_Code[3], ~OP_Code[4]);  // AND_Gate
  or or_1 (ALUsrc, MemWrite, MemRead, andi_out, ori_out, divi_out, muli_out, subi_out, addi_out);
  or or_2 (RegWrite, OP_Code[5], MemRead, andi_out, ori_out, divi_out, muli_out, subi_out, addi_out);
  or or_3 (MemToReg, MemRead, branch);
  or or_4 (ExOp, OP_Code[5], MemWrite, MemRead, branch);

  assign OP_Code_2 = OP_Code;
  assign RegDes = OP_Code[5];
endmodule
