// Logisim project Extension Unit.circ as structural Verilog: 1 circuit, main circuit main
module main (
  input  [15:0] \input ,
  input  ExOp,
  output [31:0] Result
);

  wire [31:0] bit_extender_1_out, bit_extender_2_out;

  assign bit_extender_1_out = {{16{1'b0}}, \input };  // Bit_Extender bit_extender_1
  assign bit_extender_2_out = {{16{\input [15]}}, \input };  // Bit_Extender bit_extender_2
  Multiplexer #(.width(32), .enable("false")) multiplexer_1 (
    .in0(bit_extender_1_out), .in1(bit_extender_2_out), .out(Result), .sel(ExOp));
endmodule
