// Logisim project branch unit.circ as structural Verilog: 1 circuit, main circuit main
module main (
  input  [31:0] pc,
  input  [31:0] immediate,
  input  zeroRes,
  input  branchRes,
  output [31:0] Result
);

  wire and_1_out;
  wire [31:0] adder_1_out, adder_2_out, shifter_1_out;

  Adder #(.width(32)) adder_1 (.a(32'h4), .b(pc), .out(adder_1_out));  // open: cin, cout
  Shifter #(.width(32)) shifter_1 (.in(immediate), .\dist (5'b00010), .out(shifter_1_out));
  Adder #(.width(32)) adder_2 (.a(adder_1_out), .b(shifter_1_out), .out(adder_2_out));  // open: cin, cout
  Multiplexer #(.width(32), .enable("false")) multiplexer_1 (
    .in0(adder_1_out), .in1(adder_2_out), .out(Result), .sel(and_1_out));
  and and_1 (and_1_out, zeroRes, branchRes);
endmodule
