// Logisim project jump unit.circ as structural Verilog: 1 circuit, main circuit main
module main (
  input  [31:0] \input ,
  output [31:0] jumped_Address
);

  Shifter #(.width(32)) shifter_1 (.in(\input ), .\dist (5'b00010), .out(jumped_Address));
endmodule
